# Fritzing sketch Lunchbox_Fritzing_Diagram (saved by Fritzing 0.7.12b)
stripboards: 1

parts:
  Part1 = Arduino Pro Mini 3.3V
  T1 = LM35 Temperature Sensor [package="TO92 [THT]"]
  VCC1 = Battery block 9V
  Part2 = Bar Graph Breakout Kit [package="[THT]"]

nets:
  N1: Part1.RAW, VCC1.+
  GND: Part1.GND, T1.GND, VCC1.-, Part2.GND
  VCC: Part1.VCC, T1.+Vs, Part2.+5V
  N2: Part1.A0, T1.Vout
  N3: Part1.SCK, Part2.CLKi
  N4: Part1.MOSI, Part1.D10, Part2.LATi, Part2.SIN

custom parts:
  Bar Graph Breakout Kit: Bar Graph Breakout Kit (DEV-10936)
